# Fritzing sketch 7segx3_test (saved by Fritzing 0.9.4)
breadboards: 1

parts:
  Part1 = Arduino Nano (Rev3.0)
  IC1 = IC, DIP package, 16 pins [chip_label=CB4511B]
  U1 = 74HC595 [package="DIP16 [THT]"]
  R1 = Resistor [tolerance=±5% resistance=220 package=THT]
  R2 = Resistor [tolerance=±5% resistance=220 package=THT]
  R3 = Resistor [tolerance=±5% resistance=220 package=THT]
  R4 = Resistor [tolerance=±5% resistance=220 package=THT]
  R5 = Resistor [tolerance=±5% resistance=220 package=THT]
  R6 = Resistor [tolerance=±5% resistance=220 package=THT]
  R7 = Resistor [tolerance=±5% resistance=220 package=THT]  # not connected
  U2 = 7-Segment-Display-3-Red [part_number=HS320561K package="7-Segment-3 [THT]"]
  Q1 = NPN-Transistor [package="SOT-23 [SMD]"]
  R8 = Resistor [tolerance=±5% resistance=220 package=THT]

nets:
  N1: Part1.GND, U1.OE
  N2: Part1.D6, U1.DS
  N3: Part1.D7, U1.SH_CP
  N4: Part1.D8, U1.ST_CP
  5V: Part1.5V, IC1.pin16, U1.MR, U1.VCC, R8.Pin_0
  N5: IC1.pin1, U1.Q2
  N6: IC1.pin2, U1.Q1
  N7: IC1.pin6, U1.Q0
  N8: IC1.pin7, U1.Q3
  N9: IC1.pin8, U1.GND, Q1.1
  N10: R1.Pin_1, U2.pin2
  N11: R2.Pin_1, U2.pin3
  N12: R3.Pin_0, U2.pin4
  N13: R4.Pin_0, U2.pin8
  N14: R5.Pin_0, U2.pin_10
  N15: R6.Pin_1, U2.pin_11
  N16: U2.pin5, Q1.2
  N17: Q1.0, R8.Pin_1

notes:
  Double check pins with datasheets, this has not been tested!

custom parts:
  7-Segment-Display-3-Red: 7-Segment Display 3 digits Red
