# Fritzing sketch I1 (saved by Fritzing 0.9.4)
perfboards: 1

parts:
  U1 = HDSP-433G [part_number=HDSP-433G package="7-Segment-3 [THT]"]
  U2 = HDSP-433G [part_number=HDSP-433G package="7-Segment-3 [THT]"]
  IC1 = CD4511B [chip_label=CD4511B package="DIP (Dual Inline) [THT]"]
  R1 = Resistor [tolerance=±5% resistance=220 package=THT]
  R2 = Resistor [tolerance=±5% resistance=220 package=THT]
  R3 = Resistor [tolerance=±5% resistance=220 package=THT]
  R4 = Resistor [tolerance=±5% resistance=220 package=THT]
  R5 = Resistor [tolerance=±5% resistance=220 package=THT]
  R6 = Resistor [tolerance=±5% resistance=220 package=THT]
  R7 = Resistor [tolerance=±5% resistance=220 package=THT]
  U3 = 74HC595 [package="DIP16 [THT]"]
  Q1 = NPN-Transistor Top View [package="TO92 [THT] Top View"]
  Q2 = NPN-Transistor Top View [package="TO92 [THT] Top View"]
  Q3 = NPN-Transistor Top View [package="TO92 [THT] Top View"]
  Q4 = NPN-Transistor Top View [package="TO92 [THT] Top View"]
  Q5 = NPN-Transistor Top View [package="TO92 [THT] Top View"]
  Q6 = NPN-Transistor Top View [package="TO92 [THT] Top View"]
  Q7 = NPN-Transistor Top View [package="TO92 [THT] Top View"]
  Q8 = NPN-Transistor Top View [package="TO92 [THT] Top View"]
  R8 = Resistor [tolerance=±5% resistance=220 package=THT]
  R9 = Resistor [tolerance=±5% resistance=220 package=THT]

nets:
  N1: U1.pin1, Q1.C
  N2: U1.pin3, U2.pin3, R5.Pin_1
  N3: U1.pin4, U2.pin4, R6.Pin_1, Q5.C
  N4: U1.pin5, Q3.C
  N5: U1.pin6, R8.Pin_0
  N6: U1.pin7, Q2.C
  N7: U2.pin2, R7.Pin_1, Q6.C
  N8: U2.pin_8, R2.Pin_1
  N9: U2.pin_11, R4.Pin_1
  N10: U2.pin_12, R3.Pin_1
  N11: U2.pin_15, R1.Pin_1
  N12: IC1.B, U3.Q7
  N13: IC1.C, U3.Q6
  N14: IC1.D, U3.Q2
  N15: IC1.A, U3.Q1
  N16: IC1.e, R7.Pin_0
  N17: IC1.d, R6.Pin_0
  N18: IC1.c, R5.Pin_0
  N19: IC1.b, R4.Pin_0
  N20: IC1.a, R3.Pin_0
  N21: IC1.g, R2.Pin_0
  N22: IC1.f, R1.Pin_0
  N23: U3.Q0, R9.Pin_1
  N24: Q1.E, Q2.E, Q3.E, Q7.C
  N25: Q1.B, Q6.B
  N26: Q3.B, Q4.B
  N27: Q5.E, Q6.E, Q8.E
  N28: Q5.B, R8.Pin_1
  N29: Q7.E, Q8.C
  N30: Q7.B, Q8.B, R9.Pin_0

custom parts:
  HDSP-433G: 7-Segment Display 3 digits Red
  CD4511B: BCD-to-7 segment latch decoder
  NPN-Transistor Top View: A standard NPN-transistor
