# Fritzing sketch I3 (saved by Fritzing 0.9.4)
perfboards: 1

parts:
  IC1 = CD4511B [chip_label=CD4511B package="DIP (Dual Inline) [THT]"]
  IC2 = CD4511B [chip_label=CD4511B package="DIP (Dual Inline) [THT]"]  # not connected
  U1 = 74HC595 [package="DIP16 [THT]"]
  U2 = attiny85 [package=dip]  # not connected
  Q1 = NPN-Transistor Top View [package="TO92 [THT] Top View"]
  Q2 = NPN-Transistor Top View [package="TO92 [THT] Top View"]
  Q3 = NPN-Transistor Top View [package="TO92 [THT] Top View"]
  Q4 = NPN-Transistor Top View [package="TO92 [THT] Top View"]
  R1 = Resistor [tolerance=±5% resistance=220 package=THT]  # not connected
  R2 = Resistor [tolerance=±5% resistance=220 package=THT]  # not connected
  R3 = Resistor [tolerance=±5% resistance=220 package=THT]  # not connected
  R4 = Resistor [tolerance=±5% resistance=220 package=THT]  # not connected
  R5 = Resistor [tolerance=±5% resistance=220 package=THT]  # not connected
  R6 = Resistor [tolerance=±5% resistance=220 package=THT]  # not connected
  R7 = Resistor [tolerance=±5% resistance=220 package=THT]  # not connected
  R12 = Resistor [tolerance=±5% resistance=220 package=THT]  # not connected
  R14 = Resistor [tolerance=±5% resistance=220 package=THT]  # not connected
  U3 = 7-Segment-Display-3-Red [part_number=HS320561K package="7-Segment-3 [THT]"]  # not connected
  U4 = 7-Segment-Display-3-Red [part_number=HS320561K package="7-Segment-3 [THT]"]  # not connected
  Q5 = NPN-Transistor Top View [package="TO92 [THT] Top View"]
  Q6 = NPN-Transistor Top View [package="TO92 [THT] Top View"]
  Q7 = NPN-Transistor Top View [package="TO92 [THT] Top View"]
  Q8 = NPN-Transistor Top View [package="TO92 [THT] Top View"]
  R15 = Resistor [tolerance=±5% resistance=220 package=THT]  # not connected
  R16 = Resistor [tolerance=±5% resistance=220 package=THT]  # not connected
  R17 = Resistor [tolerance=±5% resistance=220 package=THT]  # not connected
  R18 = Resistor [tolerance=±5% resistance=220 package=THT]

nets:
  N1: IC1.B, U1.Q7
  N2: IC1.C, U1.Q6
  N3: IC1.LT, IC1.BL, IC1.Vdd
  N4: IC1.D, U1.Q2
  N5: IC1.A, U1.Q1
  N6: Q1.E, Q2.E
  N7: Q1.B, Q5.B
  N8: Q3.B, Q4.B
  N9: Q5.C, Q6.C
  N10: Q7.E, Q8.C
  N11: Q7.B, Q8.B, R18.Pin_1

custom parts:
  CD4511B: BCD-to-7 segment latch decoder
  NPN-Transistor Top View: A standard NPN-transistor
  7-Segment-Display-3-Red: 7-Segment Display 3 digits Red
