# Fritzing sketch I4 (saved by Fritzing 0.9.4)
perfboards: 1

parts:
  U1 = HDSP-433G [part_number=HDSP-433G package="7-Segment-3 [THT]"]
  U2 = 74HC595 [package="DIP16 [THT]"]
  U4 = HDSP-433G [part_number=HDSP-433G package="7-Segment-3 [THT]"]
  U5 = 74HC595 [package="DIP16 [THT]"]
  Q4 = NPN-Transistor Top View [package="TO92 [THT] Top View"]
  Q5 = NPN-Transistor Top View [package="TO92 [THT] Top View"]
  Q6 = NPN-Transistor Top View [package="TO92 [THT] Top View"]
  Q7 = NPN-Transistor Top View [package="TO92 [THT] Top View"]
  Q8 = NPN-Transistor Top View [package="TO92 [THT] Top View"]
  Q9 = NPN-Transistor Top View [package="TO92 [THT] Top View"]
  R1 = Resistor [tolerance=±5% resistance=220 package=THT]  # not connected
  U6 = attiny85 [package=dip]  # not connected

nets:
  N1: U1.pin2, U4.pin2, U5.Q4
  N2: U1.pin3, U4.pin3, U5.Q3
  N3: U1.pin4, U4.pin4, U5.Q2
  N4: U1.pin_8, U4.pin_8
  N5: U1.pin_11, U2.Q1, U4.pin_11
  N6: U1.pin_12, U2.Q2, U4.pin_12
  N7: U1.pin_14, U2.Q3, U4.pin_14
  N8: U1.pin_15, U2.Q4, U4.pin_15
  N9: U2.Q5, Q9.B
  N10: U2.Q6, Q4.B
  N11: U2.Q7, Q8.B
  N12: U2.SH_CP, U5.MR
  N13: U2.ST_CP, U5.SH_CP
  N14: U4.pin6, U5.Q1
  N15: U5.Q5, Q5.B
  N16: U5.Q6, Q6.B
  N17: U5.Q7, Q7.B

custom parts:
  HDSP-433G: 7-Segment Display 3 digits Red
  NPN-Transistor Top View: A standard NPN-transistor
