# Fritzing sketch I5 (saved by Fritzing 0.9.4)
perfboards: 1
stripboards: 1

parts:
  U1 = HDSP-433G [part_number=HDSP-433G package="7-Segment-3 [THT]"]
  U2 = 74HC595 [package="DIP16 [THT]"]  # not connected
  U4 = HDSP-433G [part_number=HDSP-433G package="7-Segment-3 [THT]"]
  U5 = 74HC595 [package="DIP16 [THT]"]  # not connected
  Q4 = NPN-Transistor Top View [package="TO92 [THT] Top View"]
  Q5 = NPN-Transistor Top View [package="TO92 [THT] Top View"]
  Q6 = NPN-Transistor Top View [package="TO92 [THT] Top View"]
  Q7 = NPN-Transistor Top View [package="TO92 [THT] Top View"]
  Q8 = NPN-Transistor Top View [package="TO92 [THT] Top View"]
  Q9 = NPN-Transistor Top View [package="TO92 [THT] Top View"]
  R1 = Resistor [tolerance=±5% resistance=220 package=THT]  # not connected
  U6 = attiny85 [package=dip]  # not connected

nets:
  N1: U1.pin1, Q8.C
  N2: U1.pin5, Q4.C
  N3: U1.pin7, Q9.C
  N4: U4.pin1, Q7.C
  N5: U4.pin5, Q6.C
  N6: U4.pin7, Q5.C

custom parts:
  HDSP-433G: 7-Segment Display 3 digits Red
  NPN-Transistor Top View: A standard NPN-transistor
