# Fritzing sketch I6 (saved by Fritzing 0.9.4)
stripboards: 1

parts:
  U1 = HDSP-433G [part_number=HDSP-433G package="7-Segment-3 [THT]"]
  U2 = 74HC595 [package="DIP16 [THT]"]
  U4 = HDSP-433G [part_number=HDSP-433G package="7-Segment-3 [THT]"]
  U5 = 74HC595 [package="DIP16 [THT]"]
  Q4 = NPN-Transistor Top View [package="TO92 [THT] Top View"]
  Q5 = NPN-Transistor Top View [package="TO92 [THT] Top View"]
  Q6 = NPN-Transistor Top View [package="TO92 [THT] Top View"]
  Q7 = NPN-Transistor Top View [package="TO92 [THT] Top View"]
  Q8 = NPN-Transistor Top View [package="TO92 [THT] Top View"]
  Q9 = NPN-Transistor Top View [package="TO92 [THT] Top View"]
  U6 = attiny85 [package=dip]
  R2 = Resistor [tolerance=±5% resistance=220 package=THT]
  J1 = male pin header, 4 pins [form="♂ (male)"]

nets (from the breadboard view):
  N1: U1.pin1, Q4.C
  N2: U1.pin2, U5.Q5
  N3: U1.pin3, U5.Q4
  N4: U1.pin4, U4.pin4, U5.Q3
  N5: U1.pin5, Q9.C
  N6: U1.pin6, U5.Q2
  N7: U1.pin7, Q8.C
  N8: U1.pin_8, U5.Q1
  N9: U1.pin_11, U5.Q6
  N10: U1.pin_12, U5.Q7
  N11: U1.pin_15, U4.pin_15, U5.Q0
  GND: U2.GND, U2.OE, U5.GND, U5.OE, U6.Pin_4, R2.Pin_1, J1.pin1
  N12: U2.Q7', U5.DS
  VCC: U2.MR, U2.VCC, U5.MR, U5.VCC, U6.Pin_8, J1.pin4
  N13: U2.SH_CP, U5.SH_CP, U6.Pin_2
  N14: U2.ST_CP, U5.ST_CP, U6.Pin_3
  N15: U2.DS, U6.Pin_6
  N16: U4.pin1, Q6.E
  N17: U4.pin5, Q5.E
  N18: U4.pin7, Q7.E
  N19: Q7.C, Q9.E
  N20: U6.Pin_5, J1.pin3
  N21: U6.Pin_7, J1.pin2

custom parts:
  HDSP-433G: 7-Segment Display 3 digits Red
  NPN-Transistor Top View: A standard NPN-transistor
