# Fritzing sketch LogicLevelConverter (saved by Fritzing 0.9.4)
breadboards: 1

parts:
  Q1 = Basic FET N-Channel [package="TO220 [THT]"]
  R1 = Resistor [tolerance=±5% resistance=10k package=THT]
  R2 = Resistor [tolerance=±5% resistance=10k package=THT]
  Part1 = Arduino Leonardo (Rev3b)
  R3 = Resistor [tolerance=±5% resistance=10k package=THT]
  R4 = Resistor [tolerance=±5% resistance=10k package=THT]

nets:
  N1: Q1.gate, R1.Pin_1, Part1.3V3
  N2: Q1.drain, R2.Pin_0, Part1.SDA
  N3: Q1.source, R1.Pin_0
  N4: R2.Pin_1, Part1.5V
  N5: Part1.GND, R4.Pin_1
  N6: Part1.SCL, R3.Pin_0
  N7: R3.Pin_1, R4.Pin_0
