# Fritzing sketch LogicLevelConverter_Board (saved by Fritzing 0.9.4)
stripboards: 1

parts:
  R1 = Resistor [tolerance=±5% resistance=10k package=THT]
  R2 = Resistor [tolerance=±5% resistance=10k package=THT]
  J1 = male pin header, 4 pins [form="♂ (male)"]
  R3 = Resistor [tolerance=±5% resistance=10k package=THT]
  R4 = Resistor [tolerance=±5% resistance=10k package=THT]
  Q4 = 2N7000 FET N-Channel [part_number=2N7000 package=TO92]
  Q5 = 2N7000 FET N-Channel [part_number=2N7000 package=TO92]
  J2 = male pin header, 1 pin [form="♂ (male)"]
  J3 = male pin header, 1 pin [form="♂ (male)"]  # not connected

nets (from the schematic view):
  N1: R1.Pin_0, J1.pin4, Q4.drain
  N2: R1.Pin_1, J1.pin3, R3.Pin_1, Q4.gate, Q5.gate
  N3: R2.Pin_0, J1.pin2, Q4.source
  N4: R2.Pin_1, J1.pin1
  N5: R3.Pin_0, Q5.drain
  N6: R4.Pin_0, Q5.source
  N7: R4.Pin_1, J2.pin1

custom parts:
  2N7000 FET N-Channel: A 2N7000 MOSFET N-Channel Transistor
