# Fritzing sketch displayModuleV2 (saved by Fritzing 0.9.4)
perfboards: 1

parts:
  IC2 = CD4511B [chip_label=CD4511B package="DIP (Dual Inline) [THT]"]
  U1 = 74HC595 [package="DIP16 [THT]"]
  Q1 = NPN-Transistor Top View [package="TO92 [THT] Top View"]  # not connected
  Q2 = NPN-Transistor Top View [package="TO92 [THT] Top View"]  # not connected
  Q3 = NPN-Transistor Top View [package="TO92 [THT] Top View"]  # not connected
  R1 = Resistor [tolerance=±5% resistance=220 package=THT]  # not connected
  R2 = Resistor [tolerance=±5% resistance=220 package=THT]  # not connected
  R3 = Resistor [tolerance=±5% resistance=220 package=THT]  # not connected
  C1 = Ceramic Capacitor top view [package="100 mil [THT, multilayer]"]  # not connected
  R4 = Resistor [tolerance=±5% resistance=220 package=THT]  # not connected
  R5 = Resistor [tolerance=±5% resistance=220 package=THT]  # not connected
  R6 = Resistor [tolerance=±5% resistance=220 package=THT]  # not connected
  R7 = Resistor [tolerance=±5% resistance=220 package=THT]  # not connected
  R8 = Resistor [tolerance=±5% resistance=220 package=THT]  # not connected

nets:
  N1: IC2.B, U1.Q4
  N2: IC2.C, U1.Q5
  N3: IC2.LT, IC2.BL
  N4: IC2.LE, IC2.Vss
  N5: IC2.D, U1.Q6
  N6: IC2.A, U1.Q7

custom parts:
  CD4511B: BCD-to-7 segment latch decoder
  NPN-Transistor Top View: A standard NPN-transistor
  Ceramic Capacitor top view: 100 nF multilayer Ceramic Capacitor breadboard set to top view for perfboard use.
