# Fritzing sketch fineCoarsePots (saved by Fritzing 0.9.4)
breadboards: 1

parts:
  R1 = Rotary Potentiometer (Small) [maximum_resistance=10kΩ package=THT]
  R2 = Rotary Potentiometer (Small) [maximum_resistance=10kΩ package=THT]
  R3 = Resistor [tolerance=±5% resistance=10k package=THT]
  R4 = Resistor [tolerance=±5% resistance=100k package=THT]

nets:
  N1: R1.leg1, R2.leg1
  N2: R1.wiper, R4.Pin_0
  N3: R1.leg2, R2.leg2
  N4: R2.wiper, R3.Pin_0
  N5: R3.Pin_1, R4.Pin_1

notes:
  Pots have to have very low resistance to make them negligible
