# Fritzing sketch radioPCBv1 (saved by Fritzing 0.9.4)
perfboards: 2

parts:
  Part1 = Arduino Nano (Rev3.0)  # not connected
  J1 = female pin header, 12 pins [form="♀ (female)"]
  J2 = female pin header, 12 pins [form="♀ (female)"]
  C7 = Ceramic Capacitor [capacitance=100nF package="100 mil [THT, multilayer]"]
  J3 = screw terminal, 3 pins
  L2 = Inductor [inductance=56nH package="400 mil [THT]"]  # not connected
  C8 = Ceramic Capacitor [capacitance=1nF package="100 mil [THT, multilayer]"]
  Y2 = CRYSTAL [package=crystal-32khz-smd]  # not connected
  C9 = Ceramic Capacitor [capacitance=22pF package="100 mil [THT, multilayer]"]
  C10 = Ceramic Capacitor [capacitance=22pF package="100 mil [THT, multilayer]"]
  C11 = Ceramic Capacitor [capacitance=100nF package="100 mil [THT, multilayer]"]
  R9 = Resistor [tolerance=±5% resistance=2.2k package=THT]
  R10 = Resistor [tolerance=±5% resistance=1k package=THT]
  Q1 = NPN-Transistor Top View [package="TO92 [THT] Top View"]  # not connected
  Q2 = NPN-Transistor Top View [package="TO92 [THT] Top View"]  # not connected
  R11 = Resistor [tolerance=±5% resistance=10k package=THT]  # not connected

nets:
  N1: J1.pin4, J2.pin2, C7.0, R9.Pin_0
  N2: J1.pin5, C8.1
  N3: J1.pin8, J2.pin8
  N4: J1.pin9, J1.pin10
  N5: J2.pin3, R10.Pin_1
  N6: J2.pin6, C10.1
  N7: J2.pin7, C9.0
  N8: J2.pin10, C11.1
  N9: J3.pin3, C8.0
  N10: C9.1, C10.0

custom parts:
  NPN-Transistor Top View: A standard NPN-transistor
