# Fritzing sketch transistorDemultiplexer (saved by Fritzing 0.9.4)
breadboards: 1

parts:
  R1 = Resistor [tolerance=±5% resistance=1k package=THT]
  R2 = Resistor [tolerance=±5% resistance=1k package=THT]
  R3 = Resistor [tolerance=±5% resistance=1k package=THT]
  R10 = Resistor [tolerance=±5% resistance=1k package=THT]
  Q1 = NPN-Transistor [package="TO92 [THT]"]
  Q2 = NPN-Transistor [package="TO92 [THT]"]
  Q3 = NPN-Transistor [package="TO92 [THT]"]
  Q5 = NPN-Transistor [package="TO92 [THT]"]
  Q6 = NPN-Transistor [package="TO92 [THT]"]
  Q7 = NPN-Transistor [package="TO92 [THT]"]
  Q13 = NPN-Transistor [package="TO92 [THT]"]
  Q14 = PNP-Transistor [package="TO92 [THT]"]
  IC1 = IC, DIP package, 8 pins [chip_label=IC]
  U1 = 7-Segment-Display-3-Red [part_number=HS320561K package="7-Segment-3 [THT]"]
  U2 = 7-Segment-Display-3-Red [part_number=HS320561K package="7-Segment-3 [THT]"]
  Part1 = Arduino Nano (Rev3.0)

nets:
  N1: R1.Pin_0, Q3.B, Q7.B
  N2: R1.Pin_1, IC1.pin3
  N3: R2.Pin_0, Q2.B, Q6.B
  N4: R2.Pin_1, IC1.pin2
  N5: R3.Pin_0, Q1.B, Q5.B
  N6: R3.Pin_1, IC1.pin1
  N7: R10.Pin_0, IC1.pin4
  N8: R10.Pin_1, Q13.B, Q14.B
  N9: Q1.E, Q2.E, Q3.E, Q14.E
  N10: Q1.C, U2.pin8
  N11: Q2.C, U2.pin_9
  N12: Q3.C, U2.pin_12
  N13: Q5.E, Q6.E, Q7.E, Q13.C
  N14: Q5.C, U1.pin8
  N15: Q6.C, U1.pin_9
  N16: Q7.C, U1.pin_12
  N17: Q13.E, Q14.C, Part1.GND

custom parts:
  7-Segment-Display-3-Red: 7-Segment Display 3 digits Red
